# Fritzing sketch circuit (saved by Fritzing 0.8.7b)

parts:
  Raspberry_Pi = Raspberry Pi Zero
  hm-11_Bluetooth = Bluetooth HM-11
  Battery_Charger = TP4056 Module [part_number=HW-107]
  SPDT = SWITCH_SPDT [package=kps-1290]
  D2F1 = D2F-FL Omron Snap Action Limit Switch with Level
  BAT1 = 18650 battery holder2 [package=battery-18650-kit]
  Mod1 = 3S-BMS
  3_3v_regulator = AMS1777 5V regulator module
  Power_Led = Luxeon LED [package=luxeon]
  BAT2 = 18650 battery holder2 [package=battery-18650-kit]
  BAT3 = 18650 battery holder2 [package=battery-18650-kit]

nets:
  3V3: Raspberry_Pi.3v3, Raspberry_Pi.3V3, hm-11_Bluetooth.VCC, D2F1.NC
  GND: Raspberry_Pi.GND, hm-11_Bluetooth.GND, 3_3v_regulator.GND-_(output)
  N1: Raspberry_Pi.GIPO15, hm-11_Bluetooth.UART_RX
  N2: Raspberry_Pi.GIPO14, hm-11_Bluetooth.UART_TX
  N3: Battery_Charger.OUT-#1, 3_3v_regulator.GND-_(input), Power_Led.C
  N4: Battery_Charger.BAT-, Mod1.-
  N5: Battery_Charger.BAT+, Mod1.+
  N6: Battery_Charger.OUT-#4, SPDT.P, 3_3v_regulator.VIN+
  N7: SPDT.O, Power_Led.A
  N8: D2F1.COM, 3_3v_regulator.VOUT+
  N9: BAT1.+, Mod1.8.4V, BAT2.-
  N10: BAT1.-, Mod1.12.6V
  N11: Mod1.0V, BAT3.+
  N12: Mod1.4.2V, BAT2.+, BAT3.-

custom parts:
  TP4056 Module: TP4056 Lithium Battery Charge Management Module Links: TP4056 website
  D2F-FL Omron Snap Action Limit Switch with Level: Snap action switch with stainless steel lever.
  18650 battery holder2: 18650 Battery Holder
  3S-BMS: 3S-BMS LIPO battery charger / protection unit. Note pcb does not match the board as it will likely connect with wires, so pcb is 6 pads suitable for .1in header pins.
  AMS1777 5V regulator module: AMS1777 5V regulator module source : https://github.com/ShenTengTu/fritzing_parts/tree/master/voltage%20regulator/AMS1117_5V_regulator_module
